// Logisim project PEÕES.circ as structural Verilog: 2 circuits, main circuit CIRCUITO PEÕES
module \CIRCUITO_PEÕES  (
  input  VC,
  output S2,
  output S1,
  output S0
);

  wire and_1_out, and_2_out, and_3_out, and_4_out, and_5_out, and_6_out, and_7_out, and_8_out, and_9_out,
       and_10_out, and_11_out, and_12_out, and_13_out, and_14_out, and_15_out, and_16_out, and_17_out,
       and_18_out, and_19_out, and_20_out, bcd_display_7_1_s, bcd_display_7_1_u, bcd_display_7_1_v,
       bcd_display_7_1_w, bcd_display_7_1_x, bcd_display_7_1_y, bcd_display_7_1_z, clock_1_out, D0_q, D0_qn,
       D1_q, D1_qn, D2_q, D2_qn, D3_q, D3_qn, not_1_out, or_1_out, or_2_out, or_3_out, xor_1_out;

  not not_1 (not_1_out, VC);
  BCD_DISPLAY_7 bcd_display_7_1 (
    .A(D3_q), .B(D2_q), .C(D1_q), .D(D0_q), .x(bcd_display_7_1_x), .y(bcd_display_7_1_y),
    .z(bcd_display_7_1_z), .u(bcd_display_7_1_u), .v(bcd_display_7_1_v), .w(bcd_display_7_1_w),
    .s(bcd_display_7_1_s));
  and and_1 (and_1_out, D2_qn, D3_q);
  and and_2 (and_2_out, D3_q, D1_qn);
  and and_3 (and_3_out, D3_qn, D2_q, D1_q, D0_q);
  and and_4 (and_4_out, D1_q, D0_qn, D3_q);
  and and_5 (and_5_out, D1_qn, D2_q);
  and and_6 (and_6_out, D0_qn, D2_q);
  and and_7 (and_7_out, D1_q, D0_q, D2_qn);
  and and_8 (and_8_out, D1_q, D0_qn);
  and and_9 (and_9_out, VC, D1_qn, D0_qn);
  and and_10 (and_10_out, D2_q, D0_qn, not_1_out);
  and and_11 (and_11_out, D3_q, D0_qn, not_1_out);
  Clock clock_1 (.out(clock_1_out));
  or or_1 (or_1_out, and_1_out, and_2_out, and_3_out, and_4_out);
  or or_2 (or_2_out, and_5_out, and_6_out, and_7_out);
  xor xor_1 (xor_1_out, D1_q, D0_q);
  D_Flip_Flop D3 (.clk(clock_1_out), .D(or_1_out), .Q(D3_q), .Qn(D3_qn));  // open: preset, en, reset
  D_Flip_Flop D2 (.clk(clock_1_out), .D(or_2_out), .Q(D2_q), .Qn(D2_qn));  // open: preset, en, reset
  D_Flip_Flop D1 (.clk(clock_1_out), .D(xor_1_out), .Q(D1_q), .Qn(D1_qn));  // open: preset, en, reset
  D_Flip_Flop D0 (.clk(clock_1_out), .D(or_3_out), .Q(D0_q), .Qn(D0_qn));  // open: preset, en, reset
  or or_3 (or_3_out, and_8_out, and_9_out, and_10_out, and_11_out);
  _7_Segment_Display u_7_segment_display_1 (
    .g(bcd_display_7_1_s), .f(bcd_display_7_1_w), .a(bcd_display_7_1_x), .b(bcd_display_7_1_y),
    .e(bcd_display_7_1_v), .d(bcd_display_7_1_u), .c(bcd_display_7_1_z));  // open: dp
  and and_12 (and_12_out, D3_qn, D2_qn, D1_qn);
  and and_13 (and_13_out, D3_q, D2_q, D0_q);
  and and_14 (and_14_out, D3_q, D2_q, D1_q);
  and and_15 (and_15_out, D3_q, D2_q, D1_qn, D0_qn);
  and and_16 (and_16_out, D3_q, D2_qn, D1_q, D0_q);
  and and_17 (and_17_out, D1_q, D3_qn);
  and and_18 (and_18_out, D3_qn, D2_q);
  and and_19 (and_19_out, D1_qn, D3_q, D2_qn);
  and and_20 (and_20_out, D3_q, D2_qn, D0_qn);
  or or_4 (S2, and_12_out, and_13_out, and_14_out);
  or or_5 (S1, and_15_out, and_16_out);
  or or_6 (S0, and_17_out, and_18_out, and_19_out, and_20_out);
endmodule

module BCD_DISPLAY_7 (
  input  A,
  input  B,
  input  C,
  input  D,
  output x,
  output y,
  output z,
  output u,
  output v,
  output w,
  output s
);

  wire and_1_out, and_2_out, and_3_out, and_4_out, and_5_out, and_6_out, and_7_out, and_8_out, and_9_out,
       and_10_out, and_11_out, and_12_out, and_13_out, and_14_out, and_15_out, and_16_out, and_17_out,
       and_18_out, and_19_out, and_20_out, and_21_out, and_22_out, and_23_out, and_24_out, not_1_out,
       not_2_out, not_3_out, not_4_out, not_5_out, not_6_out, not_7_out, not_8_out, not_9_out, not_10_out,
       not_11_out, not_12_out, not_13_out, not_14_out, not_15_out, not_16_out, not_17_out, not_18_out,
       not_19_out, not_20_out, not_21_out, not_22_out, not_23_out, not_24_out, not_25_out, not_26_out,
       not_27_out, not_28_out, not_29_out, not_30_out, not_31_out, not_32_out, not_33_out, not_34_out,
       not_35_out;

  not not_1 (not_1_out, B);
  and and_1 (and_1_out, not_1_out, C, D);
  not not_2 (not_2_out, A);
  and and_2 (and_2_out, not_2_out, B, not_3_out);
  not not_3 (not_3_out, C);
  not not_4 (not_4_out, A);
  and and_3 (and_3_out, not_4_out, B, not_5_out);
  not not_5 (not_5_out, D);
  not not_6 (not_6_out, B);
  and and_4 (and_4_out, A, not_6_out, not_7_out);
  not not_7 (not_7_out, C);
  not not_8 (not_8_out, A);
  not not_9 (not_9_out, A);
  not not_10 (not_10_out, C);
  not not_11 (not_11_out, D);
  not not_12 (not_12_out, B);
  not not_13 (not_13_out, B);
  and and_5 (and_5_out, not_13_out, C, D);
  not not_14 (not_14_out, A);
  and and_6 (and_6_out, not_14_out, B);
  not not_15 (not_15_out, B);
  and and_7 (and_7_out, A, not_15_out, not_16_out);
  not not_16 (not_16_out, D);
  not not_17 (not_17_out, B);
  not not_18 (not_18_out, A);
  not not_19 (not_19_out, C);
  not not_20 (not_20_out, A);
  not not_21 (not_21_out, D);
  not not_22 (not_22_out, B);
  not not_23 (not_23_out, C);
  not not_24 (not_24_out, B);
  not not_25 (not_25_out, A);
  not not_26 (not_26_out, C);
  not not_27 (not_27_out, B);
  not not_28 (not_28_out, B);
  and and_8 (and_8_out, not_28_out, C, D);
  not not_29 (not_29_out, A);
  and and_9 (and_9_out, not_29_out, B, D);
  not not_30 (not_30_out, A);
  and and_10 (and_10_out, not_30_out, B, C);
  not not_31 (not_31_out, A);
  and and_11 (and_11_out, not_31_out, C, D);
  not not_32 (not_32_out, A);
  and and_12 (and_12_out, not_32_out, B, D);
  not not_33 (not_33_out, A);
  and and_13 (and_13_out, not_33_out, B, C);
  not not_34 (not_34_out, B);
  and and_14 (and_14_out, A, not_34_out, not_35_out);
  not not_35 (not_35_out, C);
  or or_1 (x, and_1_out, and_2_out, and_3_out, and_4_out);
  and and_15 (and_15_out, not_8_out, C, D);
  and and_16 (and_16_out, not_9_out, B, not_10_out, not_11_out);
  or or_2 (y, and_15_out, and_16_out, and_17_out);
  and and_17 (and_17_out, A, not_12_out);
  or or_3 (z, and_5_out, and_6_out, and_7_out);
  and and_18 (and_18_out, not_17_out, C, D);
  and and_19 (and_19_out, not_18_out, B, not_19_out, D);
  and and_20 (and_20_out, not_20_out, B, C, not_21_out);
  and and_21 (and_21_out, A, not_22_out, not_23_out);
  and and_22 (and_22_out, not_24_out, C, D);
  or or_4 (v, and_22_out, and_23_out, and_24_out);
  and and_23 (and_23_out, not_25_out, B, not_26_out, D);
  and and_24 (and_24_out, A, not_27_out, D);
  or or_5 (w, and_8_out, and_9_out, and_10_out);
  or or_6 (s, and_11_out, and_12_out, and_13_out, and_14_out);
  or or_7 (u, and_18_out, and_19_out, and_20_out, and_21_out);
endmodule
