// Logisim project TRABALHO FINAL - SISTEMA.circ as structural Verilog: 4 circuits, main circuit CIRCUITO PEÕES
module \CIRCUITO_PEÕES  (
  input  VC,
  output S2,
  output S1,
  output S0
);

  wire and_1_out, and_2_out, and_3_out, and_4_out, and_5_out, and_6_out, and_7_out, and_8_out, and_9_out,
       and_10_out, and_11_out, and_12_out, and_13_out, and_14_out, and_15_out, and_16_out, and_17_out,
       and_18_out, and_19_out, and_20_out, bcd_display_7_1_a_2, bcd_display_7_1_b_2, bcd_display_7_1_c_2,
       bcd_display_7_1_d_2, bcd_display_7_1_e, bcd_display_7_1_f, bcd_display_7_1_g, clock_1_out, D0_q,
       D0_qn, D1_q, D1_qn, D2_q, D2_qn, D3_q, D3_qn, not_1_out, or_1_out, or_2_out, or_3_out, xor_1_out;

  not not_1 (not_1_out, VC);
  BCD___DISPLAY_7 bcd_display_7_1 (
    .A(D3_q), .B(D2_q), .C(D1_q), .D(D0_q), .a_2(bcd_display_7_1_a_2), .b_2(bcd_display_7_1_b_2),
    .c_2(bcd_display_7_1_c_2), .d_2(bcd_display_7_1_d_2), .e(bcd_display_7_1_e), .f(bcd_display_7_1_f),
    .g(bcd_display_7_1_g));
  and and_1 (and_1_out, D2_qn, D3_q);
  and and_2 (and_2_out, D3_q, D1_qn);
  and and_3 (and_3_out, D3_qn, D2_q, D1_q, D0_q);
  and and_4 (and_4_out, D1_q, D0_qn, D3_q);
  and and_5 (and_5_out, D1_qn, D2_q);
  and and_6 (and_6_out, D0_qn, D2_q);
  and and_7 (and_7_out, D1_q, D0_q, D2_qn);
  and and_8 (and_8_out, D1_q, D0_qn);
  and and_9 (and_9_out, VC, D1_qn, D0_qn);
  and and_10 (and_10_out, D2_q, D0_qn, not_1_out);
  and and_11 (and_11_out, D3_q, D0_qn, not_1_out);
  Clock clock_1 (.out(clock_1_out));
  or or_1 (or_1_out, and_1_out, and_2_out, and_3_out, and_4_out);
  or or_2 (or_2_out, and_5_out, and_6_out, and_7_out);
  xor xor_1 (xor_1_out, D1_q, D0_q);
  D_Flip_Flop D3 (.clk(clock_1_out), .D(or_1_out), .Q(D3_q), .Qn(D3_qn));  // open: preset, en, reset
  D_Flip_Flop D2 (.clk(clock_1_out), .D(or_2_out), .Q(D2_q), .Qn(D2_qn));  // open: preset, en, reset
  D_Flip_Flop D1 (.clk(clock_1_out), .D(xor_1_out), .Q(D1_q), .Qn(D1_qn));  // open: preset, en, reset
  D_Flip_Flop D0 (.clk(clock_1_out), .D(or_3_out), .Q(D0_q), .Qn(D0_qn));  // open: preset, en, reset
  or or_3 (or_3_out, and_8_out, and_9_out, and_10_out, and_11_out);
  _7_Segment_Display u_7_segment_display_1 (
    .g(bcd_display_7_1_g), .f(bcd_display_7_1_f), .a(bcd_display_7_1_a_2), .b(bcd_display_7_1_b_2),
    .e(bcd_display_7_1_e), .d(bcd_display_7_1_d_2), .c(bcd_display_7_1_c_2));  // open: dp
  and and_12 (and_12_out, D3_qn, D2_qn, D1_qn);
  and and_13 (and_13_out, D3_q, D2_q, D0_q);
  and and_14 (and_14_out, D3_q, D2_q, D1_q);
  and and_15 (and_15_out, D3_q, D2_q, D1_qn, D0_qn);
  and and_16 (and_16_out, D3_q, D2_qn, D1_q, D0_q);
  and and_17 (and_17_out, D1_q, D3_qn);
  and and_18 (and_18_out, D3_qn, D2_q);
  and and_19 (and_19_out, D1_qn, D3_q, D2_qn);
  and and_20 (and_20_out, D3_q, D2_qn, D0_qn);
  or or_4 (S2, and_12_out, and_13_out, and_14_out);
  or or_5 (S1, and_15_out, and_16_out);
  or or_6 (S0, and_17_out, and_18_out, and_19_out, and_20_out);
endmodule

module BCD___DISPLAY_7 (
  input  A,
  input  B,
  input  C,
  input  D,
  output a_2,
  output b_2,
  output c_2,
  output d_2,
  output e,
  output f,
  output g
);

  wire and_1_out, and_2_out, and_3_out, and_4_out, and_5_out, and_6_out, and_7_out, and_8_out, and_9_out,
       and_10_out, and_11_out, and_12_out, and_13_out, and_14_out, and_15_out, and_16_out, and_17_out,
       and_18_out, and_19_out, and_20_out, and_21_out, and_22_out, and_23_out, and_24_out, not_1_out,
       not_2_out, not_3_out, not_4_out, not_5_out, not_6_out, not_7_out, not_8_out, not_9_out, not_10_out,
       not_11_out, not_12_out, not_13_out, not_14_out, not_15_out, not_16_out, not_17_out, not_18_out,
       not_19_out, not_20_out, not_21_out, not_22_out, not_23_out, not_24_out, not_25_out, not_26_out,
       not_27_out, not_28_out, not_29_out, not_30_out, not_31_out, not_32_out, not_33_out, not_34_out,
       not_35_out;

  not not_1 (not_1_out, B);
  and and_1 (and_1_out, not_1_out, C, D);
  not not_2 (not_2_out, A);
  and and_2 (and_2_out, not_2_out, B, not_3_out);
  not not_3 (not_3_out, C);
  not not_4 (not_4_out, A);
  and and_3 (and_3_out, not_4_out, B, not_5_out);
  not not_5 (not_5_out, D);
  and and_4 (and_4_out, A, not_6_out, not_7_out);
  not not_6 (not_6_out, B);
  not not_7 (not_7_out, C);
  not not_8 (not_8_out, A);
  not not_9 (not_9_out, A);
  not not_10 (not_10_out, C);
  not not_11 (not_11_out, D);
  not not_12 (not_12_out, B);
  not not_13 (not_13_out, B);
  and and_5 (and_5_out, not_13_out, C, D);
  not not_14 (not_14_out, A);
  and and_6 (and_6_out, not_14_out, B);
  not not_15 (not_15_out, B);
  and and_7 (and_7_out, A, not_15_out, not_16_out);
  not not_16 (not_16_out, D);
  not not_17 (not_17_out, B);
  not not_18 (not_18_out, A);
  not not_19 (not_19_out, C);
  not not_20 (not_20_out, A);
  not not_21 (not_21_out, D);
  not not_22 (not_22_out, B);
  not not_23 (not_23_out, C);
  not not_24 (not_24_out, B);
  not not_25 (not_25_out, A);
  not not_26 (not_26_out, C);
  not not_27 (not_27_out, B);
  not not_28 (not_28_out, B);
  and and_8 (and_8_out, not_28_out, C, D);
  not not_29 (not_29_out, A);
  and and_9 (and_9_out, not_29_out, B, D);
  not not_30 (not_30_out, A);
  and and_10 (and_10_out, not_30_out, B, C);
  not not_31 (not_31_out, A);
  and and_11 (and_11_out, not_31_out, C, D);
  not not_32 (not_32_out, A);
  and and_12 (and_12_out, not_32_out, B, D);
  not not_33 (not_33_out, A);
  and and_13 (and_13_out, not_33_out, B, C);
  not not_34 (not_34_out, B);
  and and_14 (and_14_out, A, not_34_out, not_35_out);
  not not_35 (not_35_out, C);
  or or_1 (a_2, and_1_out, and_2_out, and_3_out, and_4_out);
  and and_15 (and_15_out, not_8_out, C, D);
  and and_16 (and_16_out, not_9_out, B, not_10_out, not_11_out);
  or or_2 (b_2, and_15_out, and_16_out, and_17_out);
  and and_17 (and_17_out, A, not_12_out);
  or or_3 (c_2, and_5_out, and_6_out, and_7_out);
  and and_18 (and_18_out, not_17_out, C, D);
  and and_19 (and_19_out, not_18_out, B, not_19_out, D);
  and and_20 (and_20_out, not_20_out, B, C, not_21_out);
  and and_21 (and_21_out, A, not_22_out, not_23_out);
  and and_22 (and_22_out, not_24_out, C, D);
  and and_23 (and_23_out, not_25_out, B, not_26_out, D);
  or or_4 (e, and_22_out, and_23_out, and_24_out);
  and and_24 (and_24_out, A, not_27_out, D);
  or or_5 (f, and_8_out, and_9_out, and_10_out);
  or or_6 (g, and_11_out, and_12_out, and_13_out, and_14_out);
  or or_7 (d_2, and_18_out, and_19_out, and_20_out, and_21_out);
endmodule

module \CIRCUITO_VEÍCULOS  (
  input  B_SV,
  input  SP,
  output S2,
  output S1,
  output S0
);

  wire and_1_out, and_2_out, and_3_out, and_4_out, and_5_out, and_6_out, clock_1_out, D0_q, D0_qn, D1_q,
       D1_qn, not_1_out, or_1_out, or_2_out;

  not not_1 (not_1_out, SP);
  and and_1 (and_1_out, D1_q, D0_qn);
  and and_2 (and_2_out, D1_qn, D0_q);
  and and_3 (and_3_out, not_1_out, D0_q);
  and and_4 (and_4_out, D1_q, D0_qn);
  and and_5 (and_5_out, D1_q, not_1_out);
  and and_6 (and_6_out, D0_qn, B_SV);
  Clock clock_1 (.out(clock_1_out));
  or or_1 (or_1_out, and_1_out, and_2_out, and_3_out);
  or or_2 (or_2_out, and_4_out, and_5_out, and_6_out);
  D_Flip_Flop D1 (.clk(clock_1_out), .D(or_1_out), .Q(D1_q), .Qn(D1_qn));  // open: preset, en, reset
  D_Flip_Flop D0 (.clk(clock_1_out), .D(or_2_out), .Q(D0_q), .Qn(D0_qn));  // open: preset, en, reset
  and and_7 (S2, D1_q, D0_q);
  xor xor_1 (S1, D1_q, D0_q);
  and and_8 (S0, D1_qn, D0_qn);
endmodule

module SISTEMA_COMPLETO (
  input  \SENSOR_E_BOTÃO 
);

  wire and_1_out, \Semáforo_Peões_s0 , \Semáforo_Peões_s1 , \Semáforo_Peões_s2 , \Semáforo_Veículos_s0 ,
       \Semáforo_Veículos_s1 , \Semáforo_Veículos_s2 ;

  and and_1 (and_1_out, \Semáforo_Peões_s2 , \Semáforo_Peões_s1 , \Semáforo_Peões_s0 );
  \CIRCUITO_VEÍCULOS  \Semáforo_Veículos  (
    .B_SV(\SENSOR_E_BOTÃO ), .SP(and_1_out), .S2(\Semáforo_Veículos_s2 ), .S1(\Semáforo_Veículos_s1 ),
    .S0(\Semáforo_Veículos_s0 ));
  \CIRCUITO_PEÕES  \Semáforo_Peões  (
    .VC(\Semáforo_Veículos_s2 ), .S2(\Semáforo_Peões_s2 ), .S1(\Semáforo_Peões_s1 ), .S0(\Semáforo_Peões_s0 ));
  LED led_1 (.in(\Semáforo_Veículos_s2 ));
  LED led_2 (.in(\Semáforo_Veículos_s1 ));
  LED led_3 (.in(\Semáforo_Veículos_s0 ));
  LED led_4 (.in(\Semáforo_Peões_s2 ));
  LED led_5 (.in(\Semáforo_Peões_s1 ));
  LED led_6 (.in(\Semáforo_Peões_s0 ));
endmodule
