// Logisim project veiculos.circ as structural Verilog: 1 circuit, main circuit main
module main (
  input  B_SV,
  input  SP,
  output S2,
  output S1,
  output S0
);

  wire and_1_out, and_2_out, and_3_out, and_4_out, and_5_out, and_6_out, and_7_out, and_8_out, clock_1_out,
       D0_q, D0_qn, D1_q, D1_qn, not_1_out, or_1_out, or_2_out, xor_1_out;

  not not_1 (not_1_out, SP);
  and and_1 (and_1_out, D1_q, D0_qn);
  and and_2 (and_2_out, D1_qn, D0_q);
  and and_3 (and_3_out, not_1_out, D0_q);
  and and_4 (and_4_out, D1_q, D0_qn);
  and and_5 (and_5_out, D1_q, not_1_out);
  and and_6 (and_6_out, D0_qn, B_SV);
  Clock clock_1 (.out(clock_1_out));
  D_Flip_Flop D1 (.clk(clock_1_out), .D(or_1_out), .Q(D1_q), .Qn(D1_qn));  // open: preset, en, reset
  or or_1 (or_1_out, and_1_out, and_2_out, and_3_out);
  or or_2 (or_2_out, and_4_out, and_5_out, and_6_out);
  D_Flip_Flop D0 (.clk(clock_1_out), .D(or_2_out), .Q(D0_q), .Qn(D0_qn));  // open: preset, en, reset
  and and_7 (and_7_out, D1_q, D0_q);
  xor xor_1 (xor_1_out, D1_q, D0_q);
  LED led_1 (.in(and_7_out));
  LED led_2 (.in(xor_1_out));
  and and_8 (and_8_out, D1_qn, D0_qn);
  LED led_3 (.in(and_8_out));
endmodule
